// Logisim project Game_of_Life.circ as structural Verilog: 4 circuits, main circuit main
module main (
);

  wire A_IN, A_OUT, B_IN, B_OUT, CE, Clock, Clock_t, CO, comparator_1_eq, D_IN, DA_IN, F_IN, I_IN, I_OUT, J,
       L_IN, L_OUT, M1_IN, M2_IN, R1_IN, R1_OUT, R2_IN, R2_OUT, REFRESH, SUM_OUT, V1_IN, V2_IN;
  wire [3:0] controlled_buffer_1_out, Display_A_q, MAR_2_q;
  wire [7:0] Instruction_Register_q, MAR_1_q, PC_q;
  wire [8:0] counter_1_q;
  wire [11:0] controlled_buffer_1_out_2;
  wire [15:0] A_q, adder_1_out, B_q, display_connector_1_out_6, display_connector_1_out_7,
       display_connector_1_out_8, display_connector_1_out_9, display_connector_1_out_10,
       display_connector_1_out_11, display_connector_1_out_12, display_connector_1_out_13,
       display_connector_1_out_14, display_connector_1_out_15, display_connector_1_out_16,
       display_connector_1_out_17, display_connector_1_out_18, display_connector_1_out_19,
       display_connector_1_out_20, display_connector_1_out_21, Live_q, parallel_rule_update_16_1_out_4, V1_q,
       V2_q;
  wire [15:8] undriven;
  wire [15:13] Instruction_Register_q_2;

  Register #(.width(16)) Live (
    .D({controlled_buffer_1_out_2, controlled_buffer_1_out}), .en(L_IN), .Q(Live_q), .clk(Clock));  // open: clr
  Register #(.width(16)) V1 (
    .D({controlled_buffer_1_out_2, controlled_buffer_1_out}), .en(V1_IN), .Q(V1_q), .clk(Clock));  // open: clr
  Register #(.width(16)) V2 (
    .D({controlled_buffer_1_out_2, controlled_buffer_1_out}), .en(V2_IN), .Q(V2_q), .clk(Clock));  // open: clr
  Parallel_rule_update_16 parallel_rule_update_16_1 (
    .Live_Line(Live_q), .V_1(V1_q), .V__1(V2_q), .out_4(parallel_rule_update_16_1_out_4));
  assign {controlled_buffer_1_out_2, controlled_buffer_1_out} = L_OUT ? parallel_rule_update_16_1_out_4 : 16'bz;  // Controlled_Buffer controlled_buffer_1
  Register #(.width(4)) MAR_2 (.D(controlled_buffer_1_out), .en(M2_IN), .Q(MAR_2_q), .clk(Clock));  // open: clr
  RAM #(.addrWidth(4), .dataWidth(16), .bus("separate")) ram_1 (
    .addr(MAR_2_q), .din({controlled_buffer_1_out_2, controlled_buffer_1_out}),
    .data({controlled_buffer_1_out_2, controlled_buffer_1_out}), .str(R2_IN), .clk(Clock), .ld(R2_OUT));  // open: sel, clr
  assign {controlled_buffer_1_out_2, controlled_buffer_1_out} = A_OUT ? A_q : 16'bz;  // Controlled_Buffer controlled_buffer_2
  Register #(.width(16)) A (
    .D({controlled_buffer_1_out_2, controlled_buffer_1_out}), .en(A_IN), .Q(A_q), .clk(Clock_t));  // open: clr
  Comparator #(.width(16)) comparator_1 (.a(A_q), .b(B_q), .eq(comparator_1_eq));  // open: gt, lt
  Adder #(.width(16)) adder_1 (.a(A_q), .b(B_q), .out(adder_1_out));  // open: cin, cout
  Register #(.width(16)) B (
    .D({controlled_buffer_1_out_2, controlled_buffer_1_out}), .en(B_IN), .Q(B_q), .clk(Clock));  // open: clr
  assign {controlled_buffer_1_out_2, controlled_buffer_1_out} = B_OUT ? B_q : 16'bz;  // Controlled_Buffer controlled_buffer_3
  Counter PC (
    .load(J), .D({controlled_buffer_1_out_2[3:0], controlled_buffer_1_out}), .count(CE), .Q(PC_q), .clk(Clock));  // open: carry, clr
  assign {controlled_buffer_1_out_2, controlled_buffer_1_out} = CO ? {undriven, PC_q} : 16'bz;  // Controlled_Buffer controlled_buffer_4
  Register MAR_1 (
    .D({controlled_buffer_1_out_2[3:0], controlled_buffer_1_out}), .en(M1_IN), .Q(MAR_1_q), .clk(Clock));  // open: clr
  RAM #(.dataWidth(16), .bus("separate")) ram_2 (
    .addr(MAR_1_q), .din({controlled_buffer_1_out_2, controlled_buffer_1_out}),
    .data({controlled_buffer_1_out_2, controlled_buffer_1_out}), .str(R1_IN), .clk(Clock), .ld(R1_OUT));  // open: sel, clr
  Register #(.width(1)) FLAGS (.D(comparator_1_eq), .en(F_IN), .Q(counter_1_q[8]), .clk(Clock));  // open: clr
  assign {controlled_buffer_1_out_2, controlled_buffer_1_out} = SUM_OUT ? adder_1_out : 16'bz;  // Controlled_Buffer controlled_buffer_5
  assign {controlled_buffer_1_out_2, controlled_buffer_1_out} = I_OUT ? {{8{1'b0}}, Instruction_Register_q} : 16'bz;  // Controlled_Buffer controlled_buffer_6
  Register #(.width(16)) Instruction_Register (
    .D({controlled_buffer_1_out_2, controlled_buffer_1_out}), .en(I_IN),
    .Q({Instruction_Register_q_2, counter_1_q[7:3], Instruction_Register_q}), .clk(Clock));  // open: clr
  Clock clock_1 (.out(Clock));
  Counter #(.width(3), .max('h7)) counter_1 (.Q(counter_1_q[2:0]), .clk(Clock));  // open: load, D, count, carry, clr
  Register #(.width(4)) Display_A (.D(controlled_buffer_1_out), .en(DA_IN), .Q(Display_A_q), .clk(Clock));  // open: clr
  ROM #(.addrWidth(9), .dataWidth(24)) rom_1 (
    .addr(counter_1_q),
    .data({REFRESH, D_IN, DA_IN, F_IN, CO, CE, J, I_OUT, I_IN, L_OUT, L_IN, V2_IN, V1_IN, R2_OUT, R2_IN, M2_IN, R1_OUT, R1_IN, M1_IN, SUM_OUT, B_OUT, B_IN, A_OUT, A_IN}));  // open: sel
  display_connector display_connector_1 (
    .DATA({controlled_buffer_1_out_2, controlled_buffer_1_out}), .EN(D_IN), .ADRESS(Display_A_q),
    .CLOCK(Clock), .REFRESH(REFRESH), .out_14(display_connector_1_out_14), .out_6(display_connector_1_out_6),
    .out_15(display_connector_1_out_15), .out_7(display_connector_1_out_7),
    .out_16(display_connector_1_out_16), .out_8(display_connector_1_out_8),
    .out_17(display_connector_1_out_17), .out_9(display_connector_1_out_9),
    .out_18(display_connector_1_out_18), .out_10(display_connector_1_out_10),
    .out_19(display_connector_1_out_19), .out_11(display_connector_1_out_11),
    .out_20(display_connector_1_out_20), .out_12(display_connector_1_out_12),
    .out_21(display_connector_1_out_21), .out_13(display_connector_1_out_13));
  DotMatrix #(.inputtype("row"), .matrixcols(16), .matrixrows(16)) dotmatrix_1 (
    .row0(display_connector_1_out_14), .row1(display_connector_1_out_6), .row2(display_connector_1_out_15),
    .row3(display_connector_1_out_7), .row4(display_connector_1_out_16), .row5(display_connector_1_out_8),
    .row6(display_connector_1_out_17), .row7(display_connector_1_out_9), .row8(display_connector_1_out_18),
    .row9(display_connector_1_out_10), .row10(display_connector_1_out_19),
    .row11(display_connector_1_out_11), .row12(display_connector_1_out_20),
    .row13(display_connector_1_out_12), .row14(display_connector_1_out_21), .row15(display_connector_1_out_13));

  // Notes on the sheet:
  //   contents of rom_1 (hex, n*v repeats v):
  //   80020 48080 10020 81 4*0 80020 48080 10020 84 4*0 80020 48080 10020 42 4*0 80020 48080 10020 48 4*0
  //   80020 48080 10020 50 4*0 80020 48080 10004 11 4*0 80020 48080 10001 5*0 80020 48080 10004 5*0 80020
  //   48080 30000 5*0 80020 48080 6*0 80020 48080 10020 1a0 280 0 0 0 80020 48080 10020 180 2400 0 0 0
  //   80020 48080 10020 180 c00 0 0 0 80020 48080 10020 180 1400 0 0 0 80020 48080 10020 a0 4040 0 0 0
  //   80020 48080 10020 2000a0 400080 0 0 0 80020 48080 800000 5*0 80020 48080 100000 5*0 80020 48080 6*0
  //   80020 48080 6*0 80020 48080 6*0 80020 48080 6*0 80020 48080 6*0 80020 48080 6*0 80020 48080 6*0
  //   80020 48080 6*0 80020 48080 6*0 80020 48080 6*0 80020 48080 6*0 80020 48080 6*0 80020 48080 6*0
  //   80020 48080 6*0 80020 48080 10020 81 4*0 80020 48080 10020 84 4*0 80020 48080 10020 42 4*0 80020
  //   48080 10020 48 4*0 80020 48080 10020 50 4*0 80020 48080 10004 11 4*0 80020 48080 10001 5*0 80020
  //   48080 10004 5*0 80020 48080 30000 5*0 80020 48080 30000 5*0 80020 48080 10020 1a0 280 0 0 0 80020
  //   48080 10020 180 2400 0 0 0 80020 48080 10020 180 c00 0 0 0 80020 48080 10020 180 1400 0 0 0 80020
  //   48080 10020 a0 4040 0 0 0 80020 48080 10020 2000a0 400080 0 0 0 80020 48080 800000 5*0 80020 48080
  //   100000 5*0 80020 48080 6*0 80020 48080 6*0 80020 48080 6*0 80020 48080 6*0 80020 48080 6*0 80020
  //   48080 6*0 80020 48080 6*0 80020 48080 6*0 80020 48080 6*0 80020 48080 6*0 80020 48080 6*0 80020
  //   48080 6*0 80020 48080 6*0 80020 48080
endmodule

module rule_update (
  input  C,
  input  [7:0] V,
  output S
);

  wire and_1_out, comparator_1_eq, comparator_2_eq;
  wire [1:0] adder_1_out, adder_2_out, adder_3_out, adder_4_out, adder_5_out, adder_6_out;
  wire [2:0] adder_7_out;
  wire [2:2] adder_5_cout, adder_6_cout;
  wire [3:3] adder_7_cout;

  Adder #(.width(1)) adder_1 (.a(V[0]), .b(V[1]), .out(adder_1_out[0]), .cout(adder_1_out[1]));  // open: cin
  Adder #(.width(1)) adder_2 (.a(V[2]), .b(V[3]), .out(adder_2_out[0]), .cout(adder_2_out[1]));  // open: cin
  Adder #(.width(1)) adder_3 (.a(V[4]), .b(V[5]), .out(adder_3_out[0]), .cout(adder_3_out[1]));  // open: cin
  Adder #(.width(1)) adder_4 (.a(V[6]), .b(V[7]), .out(adder_4_out[0]), .cout(adder_4_out[1]));  // open: cin
  Adder #(.width(2)) adder_5 (
    .a(adder_1_out), .b(adder_2_out), .out(adder_5_out), .cout(adder_5_cout[2]));  // open: cin
  Adder #(.width(2)) adder_6 (
    .a(adder_3_out), .b(adder_4_out), .out(adder_6_out), .cout(adder_6_cout[2]));  // open: cin
  Adder #(.width(3)) adder_7 (
    .a({adder_5_cout[2], adder_5_out}), .b({adder_6_cout[2], adder_6_out}), .out(adder_7_out),
    .cout(adder_7_cout[3]));  // open: cin
  and and_1 (and_1_out, C, comparator_1_eq);
  Comparator #(.width(4)) comparator_1 (
    .a({adder_7_cout[3], adder_7_out}), .b(4'b0010), .eq(comparator_1_eq));  // open: gt, lt
  Comparator #(.width(4)) comparator_2 (
    .a({adder_7_cout[3], adder_7_out}), .b(4'b0011), .eq(comparator_2_eq));  // open: gt, lt
  or or_1 (S, and_1_out, comparator_2_eq);
endmodule

module Parallel_rule_update_16 (
  input  [15:0] Live_Line,
  input  [15:0] V_1,
  input  [15:0] V__1,
  output [15:0] out_4
);

  rule_update rule_update_1 (
    .C(Live_Line[0]), .V({V__1[15], V__1[1:0], V_1[15], V_1[1:0], Live_Line[15], Live_Line[1]}), .S(out_4[0]));
  rule_update rule_update_2 (.C(Live_Line[1]), .V({V__1[2:0], V_1[2:0], Live_Line[2], Live_Line[0]}), .S(out_4[1]));
  rule_update rule_update_3 (.C(Live_Line[2]), .V({V__1[3:1], V_1[3:1], Live_Line[3], Live_Line[1]}), .S(out_4[2]));
  rule_update rule_update_4 (.C(Live_Line[3]), .V({V__1[4:2], V_1[4:2], Live_Line[4], Live_Line[2]}), .S(out_4[3]));
  rule_update rule_update_5 (.C(Live_Line[4]), .V({V__1[5:3], V_1[5:3], Live_Line[5], Live_Line[3]}), .S(out_4[4]));
  rule_update rule_update_6 (.C(Live_Line[5]), .V({V__1[6:4], V_1[6:4], Live_Line[6], Live_Line[4]}), .S(out_4[5]));
  rule_update rule_update_7 (.C(Live_Line[6]), .V({V__1[7:5], V_1[7:5], Live_Line[7], Live_Line[5]}), .S(out_4[6]));
  rule_update rule_update_8 (.C(Live_Line[8]), .V({V__1[9:7], V_1[9:7], Live_Line[9], Live_Line[7]}), .S(out_4[8]));
  rule_update rule_update_9 (.C(Live_Line[7]), .V({V__1[8:6], V_1[8:6], Live_Line[8], Live_Line[6]}), .S(out_4[7]));
  rule_update rule_update_10 (.C(Live_Line[9]), .V({V__1[10:8], V_1[9:7], Live_Line[10], Live_Line[8]}), .S(out_4[9]));
  rule_update rule_update_11 (
    .C(Live_Line[10]), .V({V__1[11:9], V_1[11:9], Live_Line[11], Live_Line[9]}), .S(out_4[10]));
  rule_update rule_update_12 (
    .C(Live_Line[12]), .V({V__1[13:11], V_1[13:11], Live_Line[13], Live_Line[11]}), .S(out_4[12]));
  rule_update rule_update_13 (
    .C(Live_Line[11]), .V({V__1[12:10], V_1[12:10], Live_Line[12], Live_Line[10]}), .S(out_4[11]));
  rule_update rule_update_14 (
    .C(Live_Line[13]), .V({V__1[14:12], V_1[14:12], Live_Line[14], Live_Line[12]}), .S(out_4[13]));
  rule_update rule_update_15 (
    .C(Live_Line[14]), .V({V__1[15:13], V_1[15:13], Live_Line[15], Live_Line[13]}), .S(out_4[14]));
  rule_update rule_update_16 (
    .C(Live_Line[15]), .V({V__1[15:14], V__1[0], V_1[15:14], V_1[0], Live_Line[14], Live_Line[0]}),
    .S(out_4[15]));
endmodule

module display_connector (
  input  [15:0] DATA,
  input  EN,
  input  [3:0] ADRESS,
  input  CLOCK,
  input  REFRESH,
  output [15:0] out_6,
  output [15:0] out_7,
  output [15:0] out_8,
  output [15:0] out_9,
  output [15:0] out_10,
  output [15:0] out_11,
  output [15:0] out_12,
  output [15:0] out_13,
  output [15:0] out_14,
  output [15:0] out_15,
  output [15:0] out_16,
  output [15:0] out_17,
  output [15:0] out_18,
  output [15:0] out_19,
  output [15:0] out_20,
  output [15:0] out_21
);

  wire demultiplexer_1_out0, demultiplexer_1_out1, demultiplexer_1_out2, demultiplexer_1_out3,
       demultiplexer_1_out4, demultiplexer_1_out5, demultiplexer_1_out6, demultiplexer_1_out7,
       demultiplexer_1_out8, demultiplexer_1_out9, demultiplexer_1_out10, demultiplexer_1_out11,
       demultiplexer_1_out12, demultiplexer_1_out13, demultiplexer_1_out14, demultiplexer_1_out15;
  wire [15:0] register_1_q, register_4_q, register_5_q, register_7_q, register_9_q, register_12_q,
       register_13_q, register_15_q, register_17_q, register_20_q, register_21_q, register_23_q,
       register_25_q, register_28_q, register_29_q, register_31_q;

  Demultiplexer #(.select(4)) demultiplexer_1 (
    .out0(demultiplexer_1_out0), .out1(demultiplexer_1_out1), .out2(demultiplexer_1_out2),
    .out3(demultiplexer_1_out3), .out4(demultiplexer_1_out4), .out5(demultiplexer_1_out5),
    .out6(demultiplexer_1_out6), .out7(demultiplexer_1_out7), .out8(demultiplexer_1_out8),
    .out9(demultiplexer_1_out9), .out10(demultiplexer_1_out10), .out11(demultiplexer_1_out11),
    .out12(demultiplexer_1_out12), .out13(demultiplexer_1_out13), .out14(demultiplexer_1_out14),
    .out15(demultiplexer_1_out15), .in(EN), .sel(ADRESS));  // open: en
  Register #(.width(16)) register_1 (.D(DATA), .en(demultiplexer_1_out0), .Q(register_1_q), .clk(CLOCK));  // open: clr
  Register #(.width(16)) register_2 (.D(register_1_q), .en(REFRESH), .Q(out_14), .clk(CLOCK));  // open: clr
  Register #(.width(16)) register_3 (.D(register_4_q), .en(REFRESH), .Q(out_6), .clk(CLOCK));  // open: clr
  Register #(.width(16)) register_4 (.D(DATA), .en(demultiplexer_1_out1), .Q(register_4_q), .clk(CLOCK));  // open: clr
  Register #(.width(16)) register_5 (.D(DATA), .en(demultiplexer_1_out2), .Q(register_5_q), .clk(CLOCK));  // open: clr
  Register #(.width(16)) register_6 (.D(register_5_q), .en(REFRESH), .Q(out_15), .clk(CLOCK));  // open: clr
  Register #(.width(16)) register_7 (.D(DATA), .en(demultiplexer_1_out3), .Q(register_7_q), .clk(CLOCK));  // open: clr
  Register #(.width(16)) register_8 (.D(register_7_q), .en(REFRESH), .Q(out_7), .clk(CLOCK));  // open: clr
  Register #(.width(16)) register_9 (.D(DATA), .en(demultiplexer_1_out4), .Q(register_9_q), .clk(CLOCK));  // open: clr
  Register #(.width(16)) register_10 (.D(register_13_q), .en(REFRESH), .Q(out_8), .clk(CLOCK));  // open: clr
  Register #(.width(16)) register_11 (.D(register_9_q), .en(REFRESH), .Q(out_16), .clk(CLOCK));  // open: clr
  Register #(.width(16)) register_12 (
    .D(DATA), .en(demultiplexer_1_out6), .Q(register_12_q), .clk(CLOCK));  // open: clr
  Register #(.width(16)) register_13 (
    .D(DATA), .en(demultiplexer_1_out5), .Q(register_13_q), .clk(CLOCK));  // open: clr
  Register #(.width(16)) register_14 (.D(register_12_q), .en(REFRESH), .Q(out_17), .clk(CLOCK));  // open: clr
  Register #(.width(16)) register_15 (
    .D(DATA), .en(demultiplexer_1_out7), .Q(register_15_q), .clk(CLOCK));  // open: clr
  Register #(.width(16)) register_16 (.D(register_15_q), .en(REFRESH), .Q(out_9), .clk(CLOCK));  // open: clr
  Register #(.width(16)) register_17 (
    .D(DATA), .en(demultiplexer_1_out8), .Q(register_17_q), .clk(CLOCK));  // open: clr
  Register #(.width(16)) register_18 (.D(register_20_q), .en(REFRESH), .Q(out_10), .clk(CLOCK));  // open: clr
  Register #(.width(16)) register_19 (.D(register_17_q), .en(REFRESH), .Q(out_18), .clk(CLOCK));  // open: clr
  Register #(.width(16)) register_20 (
    .D(DATA), .en(demultiplexer_1_out9), .Q(register_20_q), .clk(CLOCK));  // open: clr
  Register #(.width(16)) register_21 (
    .D(DATA), .en(demultiplexer_1_out10), .Q(register_21_q), .clk(CLOCK));  // open: clr
  Register #(.width(16)) register_22 (.D(register_21_q), .en(REFRESH), .Q(out_19), .clk(CLOCK));  // open: clr
  Register #(.width(16)) register_23 (
    .D(DATA), .en(demultiplexer_1_out11), .Q(register_23_q), .clk(CLOCK));  // open: clr
  Register #(.width(16)) register_24 (.D(register_23_q), .en(REFRESH), .Q(out_11), .clk(CLOCK));  // open: clr
  Register #(.width(16)) register_25 (
    .D(DATA), .en(demultiplexer_1_out12), .Q(register_25_q), .clk(CLOCK));  // open: clr
  Register #(.width(16)) register_26 (.D(register_25_q), .en(REFRESH), .Q(out_20), .clk(CLOCK));  // open: clr
  Register #(.width(16)) register_27 (.D(register_28_q), .en(REFRESH), .Q(out_12), .clk(CLOCK));  // open: clr
  Register #(.width(16)) register_28 (
    .D(DATA), .en(demultiplexer_1_out13), .Q(register_28_q), .clk(CLOCK));  // open: clr
  Register #(.width(16)) register_29 (
    .D(DATA), .en(demultiplexer_1_out14), .Q(register_29_q), .clk(CLOCK));  // open: clr
  Register #(.width(16)) register_30 (.D(register_29_q), .en(REFRESH), .Q(out_21), .clk(CLOCK));  // open: clr
  Register #(.width(16)) register_31 (
    .D(DATA), .en(demultiplexer_1_out15), .Q(register_31_q), .clk(CLOCK));  // open: clr
  Register #(.width(16)) register_32 (.D(register_31_q), .en(REFRESH), .Q(out_13), .clk(CLOCK));  // open: clr
endmodule
